# Fritzing sketch shutdownd (saved by Fritzing 0.9.2b)
circuit board: 5.64444cm x 8.46667cm
breadboards: 1

parts:
  PB_SHUTDOWN = Pushbutton [package="[THT]"]
  Raspberry_Pi1 = Raspberry Pi B rev2

nets:
  N1: PB_SHUTDOWN.Pin_1, PB_SHUTDOWN.Pin_2, Raspberry_Pi1.GPIO_25
  N2: PB_SHUTDOWN.Pin_3, PB_SHUTDOWN.Pin_4, Raspberry_Pi1.GND
